# Fritzing sketch DA3Schematic (saved by Fritzing 0.9.3b)
breadboards: 1

parts:
  U1 = atmega328 [package=dip]
  IC1 = USB UART [package=ssop28db]
  T1 = LM35 Temperature Sensor [package="TO92 [THT]"]

nets:
  N1: U1.RESET, IC1.DTR
  N2: U1.D0_(RX), IC1.RXD
  N3: U1.D1_(TX), IC1.TXD
  5V: U1.VCC, U1.AVCC
  GND: U1.GND
  N4: U1.A0, T1.Vout
